# Fritzing sketch oximeter_diagram (saved by Fritzing 0.9.4)
breadboards: 1

parts:
  Componente1 = Arduino Nano 33 BLE Sense
  S1 = Pushbutton [package=THT]
  R1 = Resistor [tolerance=±5% resistance=10k package=THT]
  Grove1 = Grove OLED 128x96
  MAX30102_Sensor1 = MAX30102 Oximeter and Heart-Rate Sensor [part_number=MAX30102]  # not connected

nets:
  N1: Componente1.GND, Componente1.A7
  N2: Componente1.D2, S1.leg1, R1.Pin_1
  N3: Componente1.D11/MOSI, Componente1.+5V
  N4: Componente1.A5, Grove1.SCL
  N5: Componente1.A4, Grove1.SDA
  3V3: Componente1.3V3, S1.leg0, Grove1.VCC
  N6: R1.Pin_0, Grove1.GND

custom parts:
  Arduino Nano 33 BLE Sense: The Nano 33 BLE Sense (without headers) is Arduino’s 3.3V AI enabled board in the smallest available form factor: 45x18mm! The Arduino Nano 33 BLE Sense is a completely new board on a well-known form factor. It comes with a series of embedded sensors: 9 axis inertial sensor: what makes this board ideal for wearable devices humidity, and temperature sensor: to get highly accurate measurements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
  MAX30102 Oximeter and Heart-Rate Sensor: The MAX30102 is an integrated pulse oximetry and heart-rate monitor biosensor module. It includes internal LEDs, photodetectors, optical elements, and low-noise electronics with ambient light rejection. The MAX30102 operates on a single 1.8V power supply and a separate 3.3V power supply for the internal LEDs. Communication is through a I2C-compatible interface.
